// Logisim project nand2tetris.circ as structural Verilog
module newNOT (
  input  in1,
  output out1
);

  nand nand_1 (out1, in1, in1);
endmodule

module newAND (
  input  in1,
  input  in2,
  output out_3
);

  wire nand_1_out;

  nand nand_1 (nand_1_out, in1, in2);
  not not_1 (out_3, nand_1_out);
endmodule

module newOR (
  input  in1,
  input  in2,
  output out1
);

  wire not_1_out, not_2_out;

  not not_1 (not_1_out, in1);
  not not_2 (not_2_out, in2);
  nand nand_1 (out1, not_1_out, not_2_out);
endmodule

module newXOR (
  input  in1,
  input  in2,
  output out1
);

  wire nand_1_out, or_1_out;

  or or_1 (or_1_out, in1, in2);
  nand nand_1 (nand_1_out, in1, in2);
  and and_1 (out1, or_1_out, nand_1_out);
endmodule

module newMUX (
  input  in1,
  input  sel1,
  input  in2,
  output out1
);

  wire and_1_out, and_2_out, not_1_out;

  not not_1 (not_1_out, sel1);
  and and_1 (and_1_out, in1, sel1);
  and and_2 (and_2_out, not_1_out, in2);
  or or_1 (out1, and_1_out, and_2_out);
endmodule

module newDMUX (
  input  in1,
  input  sel1,
  output out1,
  output out2
);

  wire not_1_out;

  not not_1 (not_1_out, sel1);
  and and_1 (out1, not_1_out, in1);
  and and_2 (out2, in1, sel1);
endmodule

module newNOT16 (
  input  [15:0] in1,
  output [15:0] out1
);

  assign out1 = ~in1;  // NOT_Gate not_1, 16 bits wide
endmodule

module newAND16 (
  input  [15:0] in1,
  input  [15:0] in2,
  output [15:0] out1
);

  assign out1 = in1 & in2;  // AND_Gate and_1, 16 bits wide
endmodule

module newOR16 (
  input  [15:0] in1,
  input  [15:0] in2,
  output [15:0] out1
);

  assign out1 = in1 | in2;  // OR_Gate or_1, 16 bits wide
endmodule

module newMUX16 (
  input  [15:0] in1,
  input  [15:0] in2,
  input  sel1,
  output [15:0] out1
);

  Multiplexer #(.width(16)) multiplexer_1 (.in0(in1), .in1(in2), .out(out1), .sel(sel1));
endmodule

module newOR8WAY (
  input  in1,
  input  in2,
  input  in3,
  input  in4,
  input  in5,
  input  in6,
  input  in7,
  input  in8,
  output out1
);

  wire or_1_out, or_2_out, or_3_out, or_4_out, or_5_out, or_6_out;

  or or_1 (or_1_out, in1, in2);
  or or_2 (or_2_out, in3, in4);
  or or_3 (or_3_out, in5, in6);
  or or_4 (or_4_out, in7, in8);
  or or_5 (or_5_out, or_1_out, or_2_out);
  or or_6 (or_6_out, or_3_out, or_4_out);
  or or_7 (out1, or_5_out, or_6_out);
endmodule

module newMUX4WAY16 (
  input  [15:0] in1,
  input  [15:0] in2,
  input  [15:0] in3,
  input  [15:0] in4,
  input  [1:0] in_5,
  output [15:0] out1
);

  Multiplexer #(.select(2), .width(16)) multiplexer_1 (
    .in0(in1), .in1(in2), .in2(in3), .in3(in4), .out(out1), .sel(in_5));
endmodule

module newMUX8WAY16 (
  input  [15:0] in1,
  input  [15:0] in2,
  input  [15:0] in3,
  input  [15:0] in4,
  input  [15:0] in5,
  input  [15:0] in6,
  input  [15:0] in7,
  input  [2:0] sel1,
  input  [15:0] in8,
  output [15:0] out1
);

  Multiplexer #(.select(3), .width(16)) multiplexer_1 (
    .in0(in1), .in1(in2), .in2(in3), .in3(in4), .in4(in5), .in5(in6), .in6(in7), .in7(in8), .out(out1),
    .sel(sel1));
endmodule

module newDMUX4WAY (
  input  in1,
  input  [1:0] sel2,
  output out1,
  output out2,
  output out3,
  output out4
);

  Demultiplexer #(.select(2)) demultiplexer_1 (
    .out0(out1), .out1(out2), .out2(out3), .out3(out4), .in(in1), .sel(sel2));
endmodule

module newDMUX8WAY (
  input  in1,
  input  [2:0] sel2,
  output out1,
  output out2,
  output out3,
  output out4,
  output out5,
  output ou6,
  output out7,
  output out8
);

  Demultiplexer #(.select(3)) demultiplexer_1 (
    .out0(out1), .out1(out2), .out2(out3), .out3(out4), .out4(out5), .out5(ou6), .out6(out7), .out7(out8),
    .in(in1), .sel(sel2));
endmodule

module newHalfAdder (
  input  in1,
  input  in2,
  output sum,
  output carry
);

  xor xor_1 (sum, in1, in2);
  and and_1 (carry, in1, in2);
endmodule

module newFullAdder (
  input  in1,
  input  in2,
  input  in3,
  output sum,
  output carry
);

  wire and_1_out, and_2_out, xor_1_out;

  xor xor_1 (xor_1_out, in1, in2);
  and and_1 (and_1_out, xor_1_out, in3);
  and and_2 (and_2_out, in1, in2);
  xor xor_2 (sum, xor_1_out, in3);
  or or_1 (carry, and_1_out, and_2_out);
endmodule

module newCarryRippleAdder (
  input  [3:0] inputA,
  input  [3:0] inputB,
  output [3:0] sum,
  output overflow
);
endmodule

module newALU (
  input  zx,
  input  nx,
  input  no,
  input  [15:0] inX,
  input  [15:0] inY,
  input  f,
  input  ny,
  input  zy,
  output [15:0] out1,
  output zr,
  output ng
);

  wire not_1_out, not_2_out, or_1_out;
  wire [15:0] adder_1_out, and_1_out, and_2_out, and_3_out, bit_extender_1_out, bit_extender_2_out,
       bit_extender_3_out, bit_extender_4_out, bit_extender_5_out, multiplexer_1_out, xor_1_out, xor_2_out;

  not not_1 (not_1_out, zx);
  not not_2 (not_2_out, zy);
  assign bit_extender_1_out = {{15{not_1_out}}, not_1_out};  // Bit_Extender bit_extender_1
  assign bit_extender_2_out = {{15{not_2_out}}, not_2_out};  // Bit_Extender bit_extender_2
  assign and_1_out = bit_extender_1_out & inX;  // AND_Gate and_1, 16 bits wide
  assign and_2_out = inY & bit_extender_2_out;  // AND_Gate and_2, 16 bits wide
  assign bit_extender_3_out = {{15{nx}}, nx};  // Bit_Extender bit_extender_3
  assign bit_extender_4_out = {{15{ny}}, ny};  // Bit_Extender bit_extender_4
  assign xor_1_out = bit_extender_3_out ^ and_1_out;  // XOR_Gate xor_1, 16 bits wide
  assign xor_2_out = and_2_out ^ bit_extender_4_out;  // XOR_Gate xor_2, 16 bits wide
  assign and_3_out = xor_1_out & xor_2_out;  // AND_Gate and_3, 16 bits wide
  Adder #(.width(16)) adder_1 (.a(xor_1_out), .b(xor_2_out), .out(adder_1_out));  // open: cin, cout
  Multiplexer #(.width(16)) multiplexer_1 (.in0(and_3_out), .in1(adder_1_out), .out(multiplexer_1_out), .sel(f));
  assign bit_extender_5_out = {{15{no}}, no};  // Bit_Extender bit_extender_5
  assign {ng, out1[14:0]} = bit_extender_5_out ^ multiplexer_1_out;  // XOR_Gate xor_3, 16 bits wide
  or or_1 (or_1_out, out1[0], out1[1], out1[2], out1[3], out1[4], out1[5], out1[6], out1[7], out1[8], out1[9], out1[10], out1[11], out1[12], out1[13], out1[14], ng);
  not not_3 (zr, or_1_out);

  assign out1[15] = ng;
endmodule

module newDataFlipFlop (
  input  in_1,
  output out_2
);

  wire clock_1_out, nand_1_out, nand_2_out, nand_3_out, nand_4_out, nand_5_out, nand_6_out, nand_7_out,
       nand_8_out, nand_9_out, nand_10_out;

  Clock clock_1 (.out(clock_1_out));
  nand nand_1 (nand_1_out, in_1, in_1);
  nand nand_2 (nand_2_out, nand_1_out, clock_1_out);
  nand nand_3 (nand_3_out, clock_1_out, in_1);
  nand nand_4 (nand_4_out, clock_1_out, clock_1_out);
  nand nand_5 (nand_5_out, nand_2_out, nand_6_out);
  nand nand_6 (nand_6_out, nand_5_out, nand_3_out);
  nand nand_7 (nand_7_out, nand_6_out, nand_6_out);
  nand nand_8 (nand_8_out, nand_7_out, nand_4_out);
  nand nand_9 (nand_9_out, nand_4_out, nand_6_out);
  nand nand_10 (nand_10_out, nand_8_out, out_2);
  nand nand_11 (out_2, nand_10_out, nand_9_out);
endmodule

module newBit (
  input  input1,
  input  load,
  output out1
);

  wire clock_1_out, multiplexer_1_out;

  Multiplexer multiplexer_1 (.in0(out1), .in1(input1), .out(multiplexer_1_out), .sel(load));
  Clock clock_1 (.out(clock_1_out));
  D_Flip_Flop d_ff_1 (.D(multiplexer_1_out), .clk(clock_1_out), .Q(out1));  // open: Qn, preset, reset
endmodule

module newRegister (
  input  [15:0] input1,
  input  load,
  output [15:0] out_3
);

  wire clock_1_out;
  wire [15:0] multiplexer_1_out;

  Clock clock_1 (.out(clock_1_out));
  Multiplexer #(.width(16)) multiplexer_1 (.in0(out_3), .in1(input1), .out(multiplexer_1_out), .sel(load));
  D_Flip_Flop d_ff_1 (.D(multiplexer_1_out[0]), .clk(clock_1_out), .Q(out_3[0]));  // open: Qn, preset, reset
  D_Flip_Flop d_ff_2 (.D(multiplexer_1_out[1]), .clk(clock_1_out), .Q(out_3[1]));  // open: Qn, preset, reset
  D_Flip_Flop d_ff_3 (.D(multiplexer_1_out[2]), .clk(clock_1_out), .Q(out_3[2]));  // open: Qn, preset, reset
  D_Flip_Flop d_ff_4 (.D(multiplexer_1_out[3]), .clk(clock_1_out), .Q(out_3[3]));  // open: Qn, preset, reset
  D_Flip_Flop d_ff_5 (.D(multiplexer_1_out[4]), .clk(clock_1_out), .Q(out_3[4]));  // open: Qn, preset, reset
  D_Flip_Flop d_ff_6 (.D(multiplexer_1_out[5]), .clk(clock_1_out), .Q(out_3[5]));  // open: Qn, preset, reset
  D_Flip_Flop d_ff_7 (.D(multiplexer_1_out[6]), .clk(clock_1_out), .Q(out_3[6]));  // open: Qn, preset, reset
  D_Flip_Flop d_ff_8 (.D(multiplexer_1_out[7]), .clk(clock_1_out), .Q(out_3[7]));  // open: Qn, preset, reset
  D_Flip_Flop d_ff_9 (.D(multiplexer_1_out[8]), .clk(clock_1_out), .Q(out_3[8]));  // open: Qn, preset, reset
  D_Flip_Flop d_ff_10 (.D(multiplexer_1_out[9]), .clk(clock_1_out), .Q(out_3[9]));  // open: Qn, preset, reset
  D_Flip_Flop d_ff_11 (.D(multiplexer_1_out[10]), .clk(clock_1_out), .Q(out_3[10]));  // open: Qn, preset, reset
  D_Flip_Flop d_ff_12 (.D(multiplexer_1_out[11]), .clk(clock_1_out), .Q(out_3[11]));  // open: Qn, preset, reset
  D_Flip_Flop d_ff_13 (.D(multiplexer_1_out[12]), .clk(clock_1_out), .Q(out_3[12]));  // open: Qn, preset, reset
  D_Flip_Flop d_ff_14 (.D(multiplexer_1_out[13]), .clk(clock_1_out), .Q(out_3[13]));  // open: Qn, preset, reset
  D_Flip_Flop d_ff_15 (.D(multiplexer_1_out[14]), .clk(clock_1_out), .Q(out_3[14]));  // open: Qn, preset, reset
  D_Flip_Flop d_ff_16 (.D(multiplexer_1_out[15]), .clk(clock_1_out), .Q(out_3[15]));  // open: Qn, preset, reset
endmodule

module newRAM8 (
  input  [15:0] in1,
  input  load,
  input  [2:0] address,
  output [15:0] out_4
);

  wire clock_1_out, demultiplexer_1_out0, demultiplexer_1_out1, demultiplexer_1_out2, demultiplexer_1_out3,
       demultiplexer_1_out4, demultiplexer_1_out5, demultiplexer_1_out6, demultiplexer_1_out7;
  wire [15:0] demultiplexer_2_out0, demultiplexer_2_out1, demultiplexer_2_out2, demultiplexer_2_out3,
       demultiplexer_2_out4, demultiplexer_2_out5, demultiplexer_2_out6, demultiplexer_2_out7,
       multiplexer_1_out, register_1_q, register_2_q, register_3_q, register_4_q, register_5_q, register_6_q,
       register_7_q, register_8_q;

  Demultiplexer #(.select(3)) demultiplexer_1 (
    .out0(demultiplexer_1_out0), .out1(demultiplexer_1_out1), .out2(demultiplexer_1_out2),
    .out3(demultiplexer_1_out3), .out4(demultiplexer_1_out4), .out5(demultiplexer_1_out5),
    .out6(demultiplexer_1_out6), .out7(demultiplexer_1_out7), .in(1'b1), .sel(address));
  Multiplexer #(.width(16)) multiplexer_1 (.in0(out_4), .in1(in1), .out(multiplexer_1_out), .sel(load));
  Demultiplexer #(.select(3), .width(16)) demultiplexer_2 (
    .out0(demultiplexer_2_out0), .out1(demultiplexer_2_out1), .out2(demultiplexer_2_out2),
    .out3(demultiplexer_2_out3), .out4(demultiplexer_2_out4), .out5(demultiplexer_2_out5),
    .out6(demultiplexer_2_out6), .out7(demultiplexer_2_out7), .in(multiplexer_1_out), .sel(address));
  Clock clock_1 (.out(clock_1_out));
  Register #(.width(16)) register_1 (
    .D(demultiplexer_2_out0), .en(demultiplexer_1_out0), .clk(clock_1_out), .Q(register_1_q));  // open: clr
  Register #(.width(16)) register_2 (
    .D(demultiplexer_2_out1), .en(demultiplexer_1_out1), .clk(clock_1_out), .Q(register_2_q));  // open: clr
  Register #(.width(16)) register_3 (
    .D(demultiplexer_2_out2), .en(demultiplexer_1_out2), .clk(clock_1_out), .Q(register_3_q));  // open: clr
  Register #(.width(16)) register_4 (
    .D(demultiplexer_2_out3), .en(demultiplexer_1_out3), .clk(clock_1_out), .Q(register_4_q));  // open: clr
  Register #(.width(16)) register_5 (
    .D(demultiplexer_2_out4), .en(demultiplexer_1_out4), .clk(clock_1_out), .Q(register_5_q));  // open: clr
  Register #(.width(16)) register_6 (
    .D(demultiplexer_2_out5), .en(demultiplexer_1_out5), .clk(clock_1_out), .Q(register_6_q));  // open: clr
  Register #(.width(16)) register_7 (
    .D(demultiplexer_2_out6), .en(demultiplexer_1_out6), .clk(clock_1_out), .Q(register_7_q));  // open: clr
  Register #(.width(16)) register_8 (
    .D(demultiplexer_2_out7), .en(demultiplexer_1_out7), .clk(clock_1_out), .Q(register_8_q));  // open: clr
  Multiplexer #(.select(3), .width(16)) multiplexer_2 (
    .in0(register_1_q), .in1(register_2_q), .in2(register_3_q), .in3(register_4_q), .in4(register_5_q),
    .in5(register_6_q), .in6(register_7_q), .in7(register_8_q), .out(out_4), .sel(address));
endmodule

module newRAM64 (
  input  [15:0] in1,
  input  load,
  input  [5:0] address,
  output [15:0] out_4
);

  wire clock_1_out, demultiplexer_2_out0, demultiplexer_2_out1, demultiplexer_2_out2, demultiplexer_2_out3,
       demultiplexer_2_out4, demultiplexer_2_out5, demultiplexer_2_out6, demultiplexer_2_out7;
  wire [15:0] demultiplexer_1_out0, demultiplexer_1_out1, demultiplexer_1_out2, demultiplexer_1_out3,
       demultiplexer_1_out4, demultiplexer_1_out5, demultiplexer_1_out6, demultiplexer_1_out7,
       multiplexer_1_out, ram_1_dout, ram_2_dout, ram_3_dout, ram_4_dout, ram_5_dout, ram_6_dout, ram_7_dout,
       ram_8_dout;

  Multiplexer #(.width(16)) multiplexer_1 (.in0(out_4), .in1(in1), .out(multiplexer_1_out), .sel(load));
  Demultiplexer #(.select(3), .width(16)) demultiplexer_1 (
    .out0(demultiplexer_1_out0), .out1(demultiplexer_1_out1), .out2(demultiplexer_1_out2),
    .out3(demultiplexer_1_out3), .out4(demultiplexer_1_out4), .out5(demultiplexer_1_out5),
    .out6(demultiplexer_1_out6), .out7(demultiplexer_1_out7), .in(multiplexer_1_out), .sel(address[5:3]));
  Demultiplexer #(.select(3)) demultiplexer_2 (
    .out0(demultiplexer_2_out0), .out1(demultiplexer_2_out1), .out2(demultiplexer_2_out2),
    .out3(demultiplexer_2_out3), .out4(demultiplexer_2_out4), .out5(demultiplexer_2_out5),
    .out6(demultiplexer_2_out6), .out7(demultiplexer_2_out7), .in(1'b1), .sel(address[5:3]));
  Clock clock_1 (.out(clock_1_out));
  RAM #(.addrWidth(3), .dataWidth(16), .enables("line")) ram_1 (
    .addr(address[2:0]), .we(demultiplexer_2_out0), .clk(clock_1_out), .din(demultiplexer_1_out0),
    .dout(ram_1_dout));
  RAM #(.addrWidth(3), .dataWidth(16), .enables("line")) ram_2 (
    .addr(address[2:0]), .we(demultiplexer_2_out1), .clk(clock_1_out), .din(demultiplexer_1_out1),
    .dout(ram_2_dout));
  RAM #(.addrWidth(3), .dataWidth(16), .enables("line")) ram_3 (
    .addr(address[2:0]), .we(demultiplexer_2_out2), .clk(clock_1_out), .din(demultiplexer_1_out2),
    .dout(ram_3_dout));
  RAM #(.addrWidth(3), .dataWidth(16), .enables("line")) ram_4 (
    .addr(address[2:0]), .we(demultiplexer_2_out3), .clk(clock_1_out), .din(demultiplexer_1_out3),
    .dout(ram_4_dout));
  RAM #(.addrWidth(3), .dataWidth(16), .enables("line")) ram_5 (
    .addr(address[2:0]), .we(demultiplexer_2_out4), .clk(clock_1_out), .din(demultiplexer_1_out4),
    .dout(ram_5_dout));
  RAM #(.addrWidth(3), .dataWidth(16), .enables("line")) ram_6 (
    .addr(address[2:0]), .we(demultiplexer_2_out5), .clk(clock_1_out), .din(demultiplexer_1_out5),
    .dout(ram_6_dout));
  RAM #(.addrWidth(3), .dataWidth(16), .enables("line")) ram_7 (
    .addr(address[2:0]), .we(demultiplexer_2_out6), .clk(clock_1_out), .din(demultiplexer_1_out6),
    .dout(ram_7_dout));
  RAM #(.addrWidth(3), .dataWidth(16), .enables("line")) ram_8 (
    .addr(address[2:0]), .we(demultiplexer_2_out7), .clk(clock_1_out), .din(demultiplexer_1_out7),
    .dout(ram_8_dout));
  Multiplexer #(.select(3), .width(16)) multiplexer_2 (
    .in0(ram_1_dout), .in1(ram_2_dout), .in2(ram_3_dout), .in3(ram_4_dout), .in4(ram_5_dout),
    .in5(ram_6_dout), .in6(ram_7_dout), .in7(ram_8_dout), .out(out_4), .sel(address[5:3]));
endmodule

module newRAM512 (
  input  [15:0] in1,
  input  load,
  input  [8:0] address,
  output [15:0] out_4
);

  wire clock_1_out, demultiplexer_2_out0, demultiplexer_2_out1, demultiplexer_2_out2, demultiplexer_2_out3,
       demultiplexer_2_out4, demultiplexer_2_out5, demultiplexer_2_out6, demultiplexer_2_out7;
  wire [15:0] demultiplexer_1_out0, demultiplexer_1_out1, demultiplexer_1_out2, demultiplexer_1_out3,
       demultiplexer_1_out4, demultiplexer_1_out5, demultiplexer_1_out6, demultiplexer_1_out7,
       multiplexer_1_out, ram_1_dout, ram_2_dout, ram_3_dout, ram_4_dout, ram_5_dout, ram_6_dout, ram_7_dout,
       ram_8_dout;

  Multiplexer #(.width(16)) multiplexer_1 (.in0(out_4), .in1(in1), .out(multiplexer_1_out), .sel(load));
  Demultiplexer #(.select(3), .width(16)) demultiplexer_1 (
    .out0(demultiplexer_1_out0), .out1(demultiplexer_1_out1), .out2(demultiplexer_1_out2),
    .out3(demultiplexer_1_out3), .out4(demultiplexer_1_out4), .out5(demultiplexer_1_out5),
    .out6(demultiplexer_1_out6), .out7(demultiplexer_1_out7), .in(multiplexer_1_out), .sel(address[8:6]));
  Demultiplexer #(.select(3)) demultiplexer_2 (
    .out0(demultiplexer_2_out0), .out1(demultiplexer_2_out1), .out2(demultiplexer_2_out2),
    .out3(demultiplexer_2_out3), .out4(demultiplexer_2_out4), .out5(demultiplexer_2_out5),
    .out6(demultiplexer_2_out6), .out7(demultiplexer_2_out7), .in(1'b1), .sel(address[8:6]));
  Clock clock_1 (.out(clock_1_out));
  RAM #(.addrWidth(6), .dataWidth(16), .enables("line")) ram_1 (
    .addr(address[5:0]), .we(demultiplexer_2_out0), .clk(clock_1_out), .din(demultiplexer_1_out0),
    .dout(ram_1_dout));
  RAM #(.addrWidth(6), .dataWidth(16), .enables("line")) ram_2 (
    .addr(address[5:0]), .we(demultiplexer_2_out1), .clk(clock_1_out), .din(demultiplexer_1_out1),
    .dout(ram_2_dout));
  RAM #(.addrWidth(6), .dataWidth(16), .enables("line")) ram_3 (
    .addr(address[5:0]), .we(demultiplexer_2_out2), .clk(clock_1_out), .din(demultiplexer_1_out2),
    .dout(ram_3_dout));
  RAM #(.addrWidth(6), .dataWidth(16), .enables("line")) ram_4 (
    .addr(address[5:0]), .we(demultiplexer_2_out3), .clk(clock_1_out), .din(demultiplexer_1_out3),
    .dout(ram_4_dout));
  RAM #(.addrWidth(6), .dataWidth(16), .enables("line")) ram_5 (
    .addr(address[5:0]), .we(demultiplexer_2_out4), .clk(clock_1_out), .din(demultiplexer_1_out4),
    .dout(ram_5_dout));
  RAM #(.addrWidth(6), .dataWidth(16), .enables("line")) ram_6 (
    .addr(address[5:0]), .we(demultiplexer_2_out5), .clk(clock_1_out), .din(demultiplexer_1_out5),
    .dout(ram_6_dout));
  RAM #(.addrWidth(6), .dataWidth(16), .enables("line")) ram_7 (
    .addr(address[5:0]), .we(demultiplexer_2_out6), .clk(clock_1_out), .din(demultiplexer_1_out6),
    .dout(ram_7_dout));
  RAM #(.addrWidth(6), .dataWidth(16), .enables("line")) ram_8 (
    .addr(address[5:0]), .we(demultiplexer_2_out7), .clk(clock_1_out), .din(demultiplexer_1_out7),
    .dout(ram_8_dout));
  Multiplexer #(.select(3), .width(16)) multiplexer_2 (
    .in0(ram_1_dout), .in1(ram_2_dout), .in2(ram_3_dout), .in3(ram_4_dout), .in4(ram_5_dout),
    .in5(ram_6_dout), .in6(ram_7_dout), .in7(ram_8_dout), .out(out_4), .sel(address[8:6]));
endmodule

module newRAM4K (
  input  [15:0] in1,
  input  load,
  input  [11:0] address,
  output [15:0] out_4
);

  wire clock_1_out, demultiplexer_2_out0, demultiplexer_2_out1, demultiplexer_2_out2, demultiplexer_2_out3,
       demultiplexer_2_out4, demultiplexer_2_out5, demultiplexer_2_out6, demultiplexer_2_out7;
  wire [15:0] demultiplexer_1_out0, demultiplexer_1_out1, demultiplexer_1_out2, demultiplexer_1_out3,
       demultiplexer_1_out4, demultiplexer_1_out5, demultiplexer_1_out6, demultiplexer_1_out7,
       multiplexer_1_out, ram_1_dout, ram_2_dout, ram_3_dout, ram_4_dout, ram_5_dout, ram_6_dout, ram_7_dout,
       ram_8_dout;

  Multiplexer #(.width(16)) multiplexer_1 (.in0(out_4), .in1(in1), .out(multiplexer_1_out), .sel(load));
  Demultiplexer #(.select(3), .width(16)) demultiplexer_1 (
    .out0(demultiplexer_1_out0), .out1(demultiplexer_1_out1), .out2(demultiplexer_1_out2),
    .out3(demultiplexer_1_out3), .out4(demultiplexer_1_out4), .out5(demultiplexer_1_out5),
    .out6(demultiplexer_1_out6), .out7(demultiplexer_1_out7), .in(multiplexer_1_out), .sel(address[11:9]));
  Demultiplexer #(.select(3)) demultiplexer_2 (
    .out0(demultiplexer_2_out0), .out1(demultiplexer_2_out1), .out2(demultiplexer_2_out2),
    .out3(demultiplexer_2_out3), .out4(demultiplexer_2_out4), .out5(demultiplexer_2_out5),
    .out6(demultiplexer_2_out6), .out7(demultiplexer_2_out7), .in(1'b1), .sel(address[11:9]));
  Clock clock_1 (.out(clock_1_out));
  RAM #(.addrWidth(9), .dataWidth(16), .enables("line")) ram_1 (
    .addr(address[8:0]), .we(demultiplexer_2_out0), .clk(clock_1_out), .din(demultiplexer_1_out0),
    .dout(ram_1_dout));
  RAM #(.addrWidth(9), .dataWidth(16), .enables("line")) ram_2 (
    .addr(address[8:0]), .we(demultiplexer_2_out1), .clk(clock_1_out), .din(demultiplexer_1_out1),
    .dout(ram_2_dout));
  RAM #(.addrWidth(9), .dataWidth(16), .enables("line")) ram_3 (
    .addr(address[8:0]), .we(demultiplexer_2_out2), .clk(clock_1_out), .din(demultiplexer_1_out2),
    .dout(ram_3_dout));
  RAM #(.addrWidth(9), .dataWidth(16), .enables("line")) ram_4 (
    .addr(address[8:0]), .we(demultiplexer_2_out3), .clk(clock_1_out), .din(demultiplexer_1_out3),
    .dout(ram_4_dout));
  RAM #(.addrWidth(9), .dataWidth(16), .enables("line")) ram_5 (
    .addr(address[8:0]), .we(demultiplexer_2_out4), .clk(clock_1_out), .din(demultiplexer_1_out4),
    .dout(ram_5_dout));
  RAM #(.addrWidth(9), .dataWidth(16), .enables("line")) ram_6 (
    .addr(address[8:0]), .we(demultiplexer_2_out5), .clk(clock_1_out), .din(demultiplexer_1_out5),
    .dout(ram_6_dout));
  RAM #(.addrWidth(9), .dataWidth(16), .enables("line")) ram_7 (
    .addr(address[8:0]), .we(demultiplexer_2_out6), .clk(clock_1_out), .din(demultiplexer_1_out6),
    .dout(ram_7_dout));
  RAM #(.addrWidth(9), .dataWidth(16), .enables("line")) ram_8 (
    .addr(address[8:0]), .we(demultiplexer_2_out7), .clk(clock_1_out), .din(demultiplexer_1_out7),
    .dout(ram_8_dout));
  Multiplexer #(.select(3), .width(16)) multiplexer_2 (
    .in0(ram_1_dout), .in1(ram_2_dout), .in2(ram_3_dout), .in3(ram_4_dout), .in4(ram_5_dout),
    .in5(ram_6_dout), .in6(ram_7_dout), .in7(ram_8_dout), .out(out_4), .sel(address[11:9]));
endmodule

module newRAM16K (
  input  [15:0] in1,
  input  load,
  input  [13:0] address,
  output [15:0] out_4
);

  wire clock_1_out, demultiplexer_2_out0, demultiplexer_2_out1, demultiplexer_2_out2, demultiplexer_2_out3;
  wire [15:0] demultiplexer_1_out0, demultiplexer_1_out1, demultiplexer_1_out2, demultiplexer_1_out3,
       multiplexer_1_out, ram_1_dout, ram_2_dout, ram_3_dout, ram_4_dout;

  Multiplexer #(.width(16)) multiplexer_1 (.in0(out_4), .in1(in1), .out(multiplexer_1_out), .sel(load));
  Demultiplexer #(.select(2), .width(16)) demultiplexer_1 (
    .out0(demultiplexer_1_out0), .out1(demultiplexer_1_out1), .out2(demultiplexer_1_out2),
    .out3(demultiplexer_1_out3), .in(multiplexer_1_out), .sel(address[13:12]));
  Demultiplexer #(.select(2)) demultiplexer_2 (
    .out0(demultiplexer_2_out0), .out1(demultiplexer_2_out1), .out2(demultiplexer_2_out2),
    .out3(demultiplexer_2_out3), .in(1'b1), .sel(address[13:12]));
  Clock clock_1 (.out(clock_1_out));
  RAM #(.addrWidth(12), .dataWidth(16), .enables("line")) ram_1 (
    .addr(address[11:0]), .we(demultiplexer_2_out0), .clk(clock_1_out), .din(demultiplexer_1_out0),
    .dout(ram_1_dout));
  RAM #(.addrWidth(12), .dataWidth(16), .enables("line")) ram_2 (
    .addr(address[11:0]), .we(demultiplexer_2_out1), .clk(clock_1_out), .din(demultiplexer_1_out1),
    .dout(ram_2_dout));
  RAM #(.addrWidth(12), .dataWidth(16), .enables("line")) ram_3 (
    .addr(address[11:0]), .we(demultiplexer_2_out2), .clk(clock_1_out), .din(demultiplexer_1_out2),
    .dout(ram_3_dout));
  RAM #(.addrWidth(12), .dataWidth(16), .enables("line")) ram_4 (
    .addr(address[11:0]), .we(demultiplexer_2_out3), .clk(clock_1_out), .din(demultiplexer_1_out3),
    .dout(ram_4_dout));
  Multiplexer #(.select(2), .width(16)) multiplexer_2 (
    .in0(ram_1_dout), .in1(ram_2_dout), .in2(ram_3_dout), .in3(ram_4_dout), .out(out_4), .sel(address[13:12]));
endmodule

module newPC (
  input  load,
  input  [15:0] in1,
  input  clock1,
  input  inc,
  input  reset,
  output [15:0] out1
);

  wire [15:0] adder_1_out, multiplexer_1_out, multiplexer_2_out;

  Multiplexer #(.width(16)) multiplexer_1 (.in0(multiplexer_2_out), .in1(in1), .out(multiplexer_1_out), .sel(load));
  Register #(.width(16)) register_1 (.D(multiplexer_1_out), .clk(clock1), .Q(out1), .clr(reset));  // open: en
  Adder #(.width(16)) adder_1 (.a(out1), .b(16'h1), .out(adder_1_out));  // open: cin, cout
  Multiplexer #(.width(16)) multiplexer_2 (.in0(out1), .in1(adder_1_out), .out(multiplexer_2_out), .sel(inc));
endmodule

module newCPU (
  input  [15:0] ins,
  input  [15:0] inM,
  input  reset,
  output [15:0] outM,
  output writeM,
  output [14:0] addressM,
  output [14:0] pc
);

  wire and_1_out, and_2_out, and_3_out, clock, jeq_out, jge_out, jgt_out, jle_out, jlt_out, jmp_out, jne_out,
       ng, not_1_out, not_6_out, not_7_out, notj1, notj2, notj3, notng, notzr, or_1_out, or_2_out, or_3_out,
       or_4_out, undriven, undriven_2, zr;
  wire [0:0] registerA_q;
  wire [15:0] multiplexer_1_out, multiplexer_2_out, registerD_q;

  Clock clock_1 (.out(clock));
  not not_1 (not_1_out, ins[15]);
  or or_1 (or_1_out, ng, zr);
  and and_1 (and_1_out, ins[15], ins[5]);
  or or_2 (or_2_out, not_1_out, ins[5]);
  and jgt (jgt_out, notj1, notj2, ins[0], notng, notzr);
  and jeq (jeq_out, notj1, ins[1], notj3, zr);
  or or_3 (or_3_out, zr, notng);
  and jlt (jlt_out, ins[2], notj2, notj3, notzr, ng);
  and jmp (jmp_out, ins[0], ins[1], ins[2]);
  and jne (jne_out, ins[2], notj2, ins[0], notzr);
  and jle (jle_out, ins[2], ins[1], notj3, or_1_out);
  not not_2 (notj3, ins[0]);
  and jge (jge_out, ins[0], ins[1], notj1, or_3_out);
  Multiplexer #(.width(16)) multiplexer_1 (.in0(outM), .in1(ins), .out(multiplexer_1_out), .sel(and_1_out));
  not not_3 (notj2, ins[1]);
  not not_4 (notj1, ins[2]);
  and and_2 (and_2_out, ins[3], ins[15]);
  Register #(.width(16)) registerA (
    .D(multiplexer_1_out), .en(or_2_out), .clk(clock), .Q({addressM, registerA_q[0]}), .clr(reset));
  or or_4 (or_4_out, jgt_out, jeq_out, jge_out, jlt_out, jmp_out, jne_out, jle_out);
  Register #(.width(16)) registerD (.D(outM), .en(and_2_out), .clk(undriven), .Q(registerD_q), .clr(reset));
  Multiplexer #(.width(16)) multiplexer_2 (
    .in0({addressM, registerA_q[0]}), .in1(inM), .out(multiplexer_2_out), .sel(ins[12]));
  not not_5 (notzr, zr);
  not not_6 (not_6_out, reset);
  not not_7 (not_7_out, or_4_out);
  and and_3 (and_3_out, not_6_out, not_7_out);
  newPC15 newpc15_1 (.in1(addressM), .load(or_4_out), .clock1(undriven_2), .reset(reset), .inc(and_3_out), .out1(pc));
  newALU newalu_1 (
    .zx(ins[11]), .zy(ins[9]), .inX(registerD_q), .inY(multiplexer_2_out), .nx(ins[10]), .ny(ins[8]),
    .f(ins[7]), .no(ins[6]), .ng(ng), .zr(zr), .out1(outM));
  not not_8 (notng, ng);
  and and_4 (writeM, ins[15], ins[2]);

  // Other names for the same wires on the sheet: j3 = ins[0]; j2 = ins[1]; j1 = ins[2]
endmodule

module newPC15 (
  input  load,
  input  [14:0] in1,
  input  clock1,
  input  inc,
  input  reset,
  output [14:0] out1
);

  wire [14:0] adder_1_out, multiplexer_1_out, multiplexer_2_out;

  Multiplexer #(.width(15)) multiplexer_1 (.in0(multiplexer_2_out), .in1(in1), .out(multiplexer_1_out), .sel(load));
  Register #(.width(15)) register_1 (.D(multiplexer_1_out), .clk(clock1), .Q(out1), .clr(reset));  // open: en
  Adder #(.width(15)) adder_1 (.a(out1), .b(15'h1), .out(adder_1_out));  // open: cin, cout
  Multiplexer #(.width(15)) multiplexer_2 (.in0(out1), .in1(adder_1_out), .out(multiplexer_2_out), .sel(inc));
endmodule

module newROM32K (
  input  [14:0] in1,
  output [15:0] out1
);

  ROM #(.addrWidth(15), .dataWidth(16)) rom_1 (.addr(in1), .data(out1));
endmodule

module newScreen (
  input  [12:0] address,
  input  load,
  input  clock,
  input  [15:0] in1,
  output [15:0] out1
);

  RAM #(.addrWidth(13), .dataWidth(16)) ram_1 (
    .addr(address), .we(load), .oe(1'b1), .clk(clock), .din(in1), .dout(out1));
endmodule

module newKeyboard (
  output [15:0] out1
);

  wire undriven;

  Keyboard keyboard_1 (.clk(undriven), .data(out1[6:0]));  // open: re, clr, avail

  assign out1[15:7] = 9'h1;
endmodule
